// Logisim project sCPU.circ as structural Verilog: 1 circuit, main circuit main
module main (
  output [7:0] out_1
);

  wire and_1_out, and_2_out, and_3_out, and_4_out, and_5_out, clk_out, comparator_1_eq, decoder_1_out0,
       decoder_1_out2, decoder_1_out3, decoder_2_out0, decoder_2_out1, decoder_2_out2, decoder_2_out3,
       not_1_out, RegWrite_out, rst_out;
  wire [1:0] multiplexer_3_out;
  wire [7:0] adder_1_out, adder_2_out, bit_extender_1_out, bit_extender_2_out, multiplexer_1_out,
       multiplexer_2_out, multiplexer_4_out, multiplexer_6_out, multiplexer_7_out, PC_q, r0_q, r1_q, r2_q,
       r3_q;

  Register PC (.D(multiplexer_1_out), .en(1'b1), .clk(clk_out), .Q(PC_q), .clr(rst_out));
  Adder adder_1 (.a(PC_q), .b(8'h1), .out(adder_1_out), .cin(1'b0));  // open: cout
  Multiplexer #(.width(8)) multiplexer_1 (
    .in0(adder_1_out), .in1(bit_extender_1_out), .out(multiplexer_1_out), .sel(and_1_out));
  not not_1 (not_1_out, comparator_1_eq);
  Comparator comparator_1 (.a(multiplexer_2_out), .b(multiplexer_4_out), .eq(comparator_1_eq));  // open: gt, lt
  and and_1 (and_1_out, decoder_1_out3, not_1_out);
  Multiplexer #(.select(2), .width(8)) multiplexer_2 (
    .in0(r0_q), .in1(r1_q), .in2(r2_q), .in3(r3_q), .out(multiplexer_2_out), .sel(out_1[1:0]));
  Multiplexer #(.width(2)) multiplexer_3 (.in0(out_1[3:2]), .in1(2'b00), .out(multiplexer_3_out), .sel(decoder_1_out3));
  Multiplexer #(.select(2), .width(8)) multiplexer_4 (
    .in0(r0_q), .in1(r1_q), .in2(r2_q), .in3(r3_q), .out(multiplexer_4_out), .sel(multiplexer_3_out));
  Multiplexer #(.select(3), .width(8)) multiplexer_5 (
    .in0(8'h8a), .in1(8'h90), .in2(8'ha0), .in3(8'hb1), .in4(8'h17), .in5(8'h29), .in6(8'hd1), .in7(8'hdf),
    .out(out_1), .sel(PC_q[2:0]));
  // Probe on PC_q
  Decoder #(.enable("false"), .select(2)) decoder_1 (
    .out0(decoder_1_out0), .out2(decoder_1_out2), .out3(decoder_1_out3), .sel(out_1[7:6]));  // open: out1
  Decoder #(.enable("false"), .select(2)) decoder_2 (
    .out0(decoder_2_out0), .out1(decoder_2_out1), .out2(decoder_2_out2), .out3(decoder_2_out3),
    .sel(out_1[5:4]));
  // Probe on multiplexer_2_out
  // Probe on out_1[5:4]
  assign bit_extender_1_out = {{4{1'b0}}, out_1[5:2]};  // Bit_Extender bit_extender_1
  Button rst (.out(rst_out));
  or RegWrite (RegWrite_out, decoder_1_out0, decoder_1_out2);
  Adder adder_2 (.a(multiplexer_2_out), .b(multiplexer_4_out), .out(adder_2_out), .cin(1'b0));  // open: cout
  // Probe on bit_extender_2_out
  assign bit_extender_2_out = {{4{1'b0}}, out_1[3:0]};  // Bit_Extender bit_extender_2
  Clock clk (.out(clk_out));
  // Probe on RegWrite_out
  and and_2 (and_2_out, decoder_2_out0, RegWrite_out);
  Multiplexer #(.width(8)) multiplexer_6 (
    .in0(bit_extender_2_out), .in1(adder_2_out), .out(multiplexer_6_out), .sel(decoder_1_out0));
  // Probe on multiplexer_6_out
  Multiplexer #(.width(8)) multiplexer_7 (
    .in0(bit_extender_2_out), .in1(multiplexer_6_out), .out(multiplexer_7_out), .sel(decoder_1_out0));
  Register r0 (.D(multiplexer_7_out), .en(and_2_out), .clk(clk_out), .Q(r0_q), .clr(rst_out));
  // Probe on multiplexer_7_out
  and and_3 (and_3_out, decoder_2_out1, RegWrite_out);
  Register r1 (.D(multiplexer_7_out), .en(and_3_out), .clk(clk_out), .Q(r1_q), .clr(rst_out));
  and and_4 (and_4_out, decoder_2_out2, RegWrite_out);
  Register r2 (.D(multiplexer_7_out), .en(and_4_out), .clk(clk_out), .Q(r2_q), .clr(rst_out));
  and and_5 (and_5_out, decoder_2_out3, RegWrite_out);
  Register r3 (.D(multiplexer_7_out), .en(and_5_out), .clk(clk_out), .Q(r3_q), .clr(rst_out));

  // Notes on the sheet:
  //   0: is_add
  //   1:x
  //   2:is_li
  //   3:is_bner
  //   addr[3:0]
  //   WriteBack
endmodule
