// Logisim project sCPU_enhanced.circ as structural Verilog: 1 circuit, main circuit main
module main (
  input  [7:0] instruct,
  output [7:0] out_2
);

  wire and_1_out, and_2_out, and_3_out, and_4_out, and_5_out, and_6_out, and_7_out, and_8_out, clk_out,
       comparator_1_eq, decoder_1_out0, decoder_1_out1, decoder_2_out0, decoder_2_out1, decoder_2_out2,
       decoder_2_out3, decoder_3_out0, decoder_3_out1, decoder_3_out2, decoder_3_out3, ledbar_1_p3,
       not_1_out, not_2_out, or_1_out, RegWrite_out, rst_out;
  wire [1:0] multiplexer_2_out, multiplexer_4_out;
  wire [3:0] register_1_q, register_1_q_2;
  wire [7:0] adder_1_out, adder_2_out, adder_3_out, bit_extender_1_out, bit_extender_2_out, dipswitch_1_sw1,
       LED_Data_q, multiplexer_1_out, multiplexer_3_out, multiplexer_5_out, multiplexer_7_out,
       multiplexer_8_out, multiplexer_9_out, PC_q, r0_q, r1_q, r2_q, r3_q, shifter_1_out, undriven;

  Adder adder_1 (.a(PC_q), .b(8'h1), .out(adder_1_out), .cin(1'b0));  // open: cout
  Adder adder_2 (.a(PC_q), .b(bit_extender_1_out), .out(adder_2_out), .cin(1'b0));  // open: cout
  // Probe on adder_2_out
  Register PC (.D(multiplexer_1_out), .en(1'b1), .clk(clk_out), .Q(PC_q), .clr(rst_out));
  Multiplexer #(.width(8)) multiplexer_1 (
    .in0(adder_1_out), .in1(adder_2_out), .out(multiplexer_1_out), .sel(and_1_out));
  not not_1 (not_1_out, comparator_1_eq);
  Comparator comparator_1 (.a(multiplexer_3_out), .b(multiplexer_5_out), .eq(comparator_1_eq));  // open: gt, lt
  and and_1 (and_1_out, decoder_2_out3, not_1_out);
  // Probe on and_1_out
  // Probe on out_2[2:0]
  Multiplexer #(.width(2)) multiplexer_2 (
    .in0(out_2[1:0]), .in1(out_2[5:4]), .out(multiplexer_2_out), .sel(decoder_2_out1));
  Multiplexer #(.select(2), .width(8)) multiplexer_3 (
    .in0(r0_q), .in1(r1_q), .in2(r2_q), .in3(r3_q), .out(multiplexer_3_out), .sel(multiplexer_2_out));
  Multiplexer #(.width(2)) multiplexer_4 (.in0(out_2[3:2]), .in1(2'b00), .out(multiplexer_4_out), .sel(decoder_2_out3));
  // Probe on decoder_1_out0
  // Probe on decoder_1_out1
  Decoder #(.enable("false"), .select(3)) decoder_1 (
    .out0(decoder_1_out0), .out1(decoder_1_out1), .sel(out_2[2:0]));  // open: out2, out3, out4, out5, out6, out7
  // Probe on dipswitch_1_sw1
  DipSwitch dipswitch_1 (
    .sw1(dipswitch_1_sw1[0]), .sw2(dipswitch_1_sw1[1]), .sw3(dipswitch_1_sw1[2]), .sw4(dipswitch_1_sw1[3]),
    .sw5(dipswitch_1_sw1[4]), .sw6(dipswitch_1_sw1[5]), .sw7(dipswitch_1_sw1[6]), .sw8(dipswitch_1_sw1[7]));
  Multiplexer #(.select(2), .width(8)) multiplexer_5 (
    .in0(r0_q), .in1(r1_q), .in2(r2_q), .in3(r3_q), .out(multiplexer_5_out), .sel(multiplexer_4_out));
  Multiplexer #(.select(3), .width(8)) multiplexer_6 (
    .in0(8'h40), .in1(8'hb1), .in2(8'h17), .in3(8'h29), .in4(8'hf9), .in5(8'h69), .in6({8{1'b0}}),
    .in7({8{1'b0}}), .out(out_2), .sel(PC_q[2:0]));
  // Probe on PC_q
  // Probe on bit_extender_1_out
  Decoder #(.enable("false"), .select(2)) decoder_2 (
    .out0(decoder_2_out0), .out1(decoder_2_out1), .out2(decoder_2_out2), .out3(decoder_2_out3),
    .sel(out_2[7:6]));
  Decoder #(.enable("false"), .select(2)) decoder_3 (
    .out0(decoder_3_out0), .out1(decoder_3_out1), .out2(decoder_3_out2), .out3(decoder_3_out3),
    .sel(out_2[5:4]));
  // Probe on out_2[1:0]
  // Probe on multiplexer_3_out
  // Probe on out_2[5:4]
  // Probe on out_2[1:0]
  assign bit_extender_1_out = {{4{out_2[5]}}, out_2[5:2]};  // Bit_Extender bit_extender_1
  Button rst (.out(rst_out));
  // Probe on out_2[3]
  or RegWrite (RegWrite_out, decoder_2_out0, decoder_2_out2);
  Adder adder_3 (.a(multiplexer_3_out), .b(multiplexer_5_out), .out(adder_3_out), .cin(1'b0));  // open: cout
  // Probe on undriven
  assign bit_extender_2_out = {{6{1'b0}}, out_2[1:0]};  // Bit_Extender bit_extender_2
  Clock clk (.out(clk_out));
  and and_2 (and_2_out, decoder_2_out1, out_2[3]);
  not not_2 (not_2_out, out_2[3]);
  // Probe on or_1_out
  or or_1 (or_1_out, and_6_out, RegWrite_out);
  and and_3 (and_3_out, decoder_3_out0, or_1_out);
  Multiplexer #(.width(8)) multiplexer_7 (
    .in0(undriven), .in1(adder_3_out), .out(multiplexer_7_out), .sel(decoder_2_out0));
  // Probe on multiplexer_7_out
  // Probe on multiplexer_9_out
  Multiplexer #(.width(8)) multiplexer_8 (
    .in0(shifter_1_out), .in1(multiplexer_7_out), .out(multiplexer_8_out), .sel(decoder_2_out0));
  Register r0 (.D(multiplexer_9_out), .en(and_3_out), .clk(clk_out), .Q(r0_q), .clr(rst_out));
  Multiplexer #(.width(8)) multiplexer_9 (
    .in0(multiplexer_8_out), .in1(dipswitch_1_sw1), .out(multiplexer_9_out), .sel(and_6_out));
  Shifter shifter_1 (.in(bit_extender_2_out), .\dist ({out_2[3:2], 1'b0}), .out(shifter_1_out));
  and and_4 (and_4_out, and_2_out, decoder_1_out0);
  and and_5 (and_5_out, decoder_1_out1, and_2_out);
  and and_6 (and_6_out, decoder_1_out0, not_2_out, decoder_2_out1);
  and and_7 (and_7_out, decoder_3_out1, or_1_out);
  Register r1 (.D(multiplexer_9_out), .en(and_7_out), .clk(clk_out), .Q(r1_q), .clr(rst_out));
  // Probe on and_4_out
  and and_8 (and_8_out, decoder_3_out2, or_1_out);
  Register r2 (.D(multiplexer_9_out), .en(and_8_out), .clk(clk_out), .Q(r2_q), .clr(rst_out));
  Register LED_Data (.D(multiplexer_3_out), .en(and_4_out), .clk(clk_out), .Q(LED_Data_q), .clr(rst_out));
  Register register_1 (
    .D(multiplexer_3_out), .en(and_5_out), .clk(clk_out), .Q({register_1_q_2, register_1_q}), .clr(rst_out));
  // LedBar #(.inputtype("row")) ledbar_1: pin names not known; wires that end beside it: rst_out, LED_Data_q, ledbar_1_p3, rst_out, multiplexer_9_out, clk_out, rst_out
  Hex_Digit_Display #(.decimalPoint("false")) hex_digit_display_1 (.value(register_1_q_2));
  and and_9 (ledbar_1_p3, decoder_3_out3, or_1_out);
  Register r3 (.D(multiplexer_9_out), .en(ledbar_1_p3), .clk(clk_out), .Q(r3_q), .clr(rst_out));
  Hex_Digit_Display #(.decimalPoint("false")) hex_digit_display_2 (.value(register_1_q));

  // Notes on the sheet:
  //   opcode
  //   2|2|1|3
  //   rd
  //   io
  //   idx
  //   out_not_equal
  //   0: is_add
  //   1:is_io
  //   2:is_li
  //   3:is_bner
  //   addr[3:0]
  //   WriteBack
  //   HEXWrite
  //   IOInputWrite
  //   idx=000
  //   idx=001
endmodule
